# Fritzing sketch Arduino_Arduino_CAN (saved by Fritzing 0.9.4)
breadboards: 1

parts:
  A1 = Arduino UNO R4 WiFi
  A2 = Arduino UNO R4 WiFi
  R2 = Resistor [tolerance=±5% resistance=10k package=THT]
  R3 = Resistor [tolerance=±5% resistance=10k package=THT]
  R4 = Resistor [tolerance=±5% resistance=10k package=THT]
  M1 = SN65HVD230 CAN Bus transciever module [package=THT]
  M2 = SN65HVD230 CAN Bus transciever module [package=THT]
  R5 = Resistor [tolerance=±5% resistance=10k package=THT]
  R6 = Resistor [tolerance=±5% resistance=10k package=THT]
  R7 = Resistor [tolerance=±5% resistance=10k package=THT]

nets:
  N1: A1.Pin_7, A1.Pin_19, M2.pin_1
  N2: A1.Pin_9, A1.Pin_10, A1.Pin_25, A2.Pin_2, A2.Pin_10, A2.Pin_30, R2.Pin_1, M1.pin_2, M2.pin_2, R7.Pin_0
  N3: A1.Pin_38, R5.Pin_1
  N4: A1.Pin_39, M2.pin_4
  N5: A2.Pin_7, A2.Pin_19, M1.pin_1
  N6: A2.Pin_38, R3.Pin_0
  N7: A2.Pin_39, M1.pin_4
  N8: R2.Pin_0, R4.Pin_1
  N9: R3.Pin_1, R4.Pin_0, M1.pin_3
  N10: M2.pin_3, R5.Pin_0, R6.Pin_1
  N11: R6.Pin_0, R7.Pin_1

custom parts:
  Arduino UNO R4 WiFi: The Arduino UNO R4 WiFi merges the RA4M1 microprocessor from Renesas with the ESP32-S3 from Espressif, creating an all-in-one tool for makers with enhanced processing power and a diverse array of new peripherals.
  SN65HVD230 CAN Bus transciever module: Bus Transceiver SN65HVD230 CAN Communication Module, for Arduino.
