# Fritzing sketch Arduino_Cubemars (saved by Fritzing 0.9.4)
breadboards: 1

parts:
  A2 = Arduino UNO R4 WiFi
  M3 = SN65HVD230 CAN Bus transciever module [package=THT]
  R1 = Resistor [tolerance=±5% resistance=220 package=THT]
  R2 = Resistor [tolerance=±5% resistance=220 package=THT]
  R3 = Resistor [tolerance=±5% resistance=220 package=THT]

nets:
  N1: A2.Pin_7, A2.Pin_19, M3.pin_1
  N2: A2.Pin_9, A2.Pin_18, A2.Pin_25, M3.pin_2, R1.Pin_1
  N3: A2.Pin_44, R3.Pin_0
  N4: A2.Pin_47, M3.pin_4
  N5: M3.pin_3, R2.Pin_0, R3.Pin_1
  N6: R1.Pin_0, R2.Pin_1

notes:
  BLUE=CANL
  WHITE=CANH
  Must connect UART GND to Arduino GND

custom parts:
  Arduino UNO R4 WiFi: The Arduino UNO R4 WiFi merges the RA4M1 microprocessor from Renesas with the ESP32-S3 from Espressif, creating an all-in-one tool for makers with enhanced processing power and a diverse array of new peripherals.
  SN65HVD230 CAN Bus transciever module: Bus Transceiver SN65HVD230 CAN Communication Module, for Arduino.
