# Fritzing sketch Arduino_Teensy_CAN (saved by Fritzing 0.9.4)
breadboards: 1

parts:
  Teensy1 = Teensy 4.1
  M2 = SN65HVD230 CAN Bus transciever module [package=THT]
  A3 = Arduino UNO R4 WiFi
  M3 = SN65HVD230 CAN Bus transciever module [package=THT]
  R5 = Resistor [tolerance=±5% resistance=10k package=THT]
  R6 = Resistor [tolerance=±5% resistance=10k package=THT]
  R7 = Resistor [tolerance=±5% resistance=10k package=THT]

nets:
  N1: Teensy1.A7/D21, M2.pin_4
  N2: Teensy1.A8/D22, M2.pin_3
  N3: Teensy1.3V3_LOW, M2.pin_1
  N4: Teensy1.GND2, M2.pin_2, A3.Pin_9, A3.Pin_10, A3.Pin_30, A3.Pin_48, M3.pin_2, R6.Pin_0
  N5: M2.pin_5, M3.pin_5
  N6: M2.pin_6, M3.pin_6
  N7: A3.Pin_7, A3.Pin_19, M3.pin_1
  N8: A3.Pin_38, R5.Pin_1
  N9: A3.Pin_39, M3.pin_4
  N10: M3.pin_3, R5.Pin_0, R7.Pin_1
  N11: R6.Pin_1, R7.Pin_0

notes:
  D22 = CANTX
  D23 = CANRX
  Using CAN1 on the Teensy
  For Arduino R4
  D5 = CRX
  D4 = CANTX

custom parts:
  Teensy 4.1: The Teensy is a complete USB-based microcontoller development system, in a very small footprint, capable of implementing many types of projects. All programming is done via the USB port. No special programmer is needed, only a standard micro-USB cable and a PC or Macintosh with a USB port.
  SN65HVD230 CAN Bus transciever module: Bus Transceiver SN65HVD230 CAN Communication Module, for Arduino.
  Arduino UNO R4 WiFi: The Arduino UNO R4 WiFi merges the RA4M1 microprocessor from Renesas with the ESP32-S3 from Espressif, creating an all-in-one tool for makers with enhanced processing power and a diverse array of new peripherals.
