# Fritzing sketch wiring_Teensy (saved by Fritzing 0.9.4)

parts:
  M1 = SN65HVD230 CAN Bus transciever module [package=THT]
  R1 = Resistor [tolerance=±5% resistance=120 package=THT]
  R2 = Resistor [tolerance=±5% resistance=10k package="2512 [SMD]"]
  R3 = Resistor [tolerance=±5% resistance=10k package="2512 [SMD]"]
  R4 = Resistor [tolerance=±5% resistance=10k package="2512 [SMD]"]
  Teensy1 = Teensy 4.1

nets:
  N1: M1.pin_1, Teensy1.3V3_LOW
  N2: M1.pin_2, Teensy1.GND2#31
  N3: M1.pin_3, Teensy1.A8/D22
  N4: M1.pin_4, Teensy1.A9/D23
  N5: M1.pin_5, R1.Pin_0
  N6: M1.pin_6, R1.Pin_1
  N7: R2.Pin_0, Teensy1.GND, Teensy1.GND2#55
  N8: R2.Pin_1, R3.Pin_0
  N9: R3.Pin_1, R4.Pin_0, Teensy1.D1

notes:
  as a safety, cut the VIN header pin of the teensy so that the teensy is always powered from USB. This avoids cutting the VUSB/VBOARD pad bridge while ensuring safe voltage
  MISO1 (D1)
  CSB_L (D0)
  CSB_R (D9)
  MOSI1 (D26)
  SCK (D27)
  CANRX (D23)
  CANTX (D22)
  TRQ_L_1 (D41)
  GND for COM
  TRQ_L_2 (D16)
  TRQ_R_2 (D17)
  TRQ_R_1 (D21)

custom parts:
  SN65HVD230 CAN Bus transciever module: Bus Transceiver SN65HVD230 CAN Communication Module, for Arduino.
  Teensy 4.1: The Teensy is a complete USB-based microcontoller development system, in a very small footprint, capable of implementing many types of projects. All programming is done via the USB port. No special programmer is needed, only a standard micro-USB cable and a PC or Macintosh with a USB port.
